# Fritzing sketch AutoWaterFlower (saved by Fritzing 0.9.0b)
breadboards: 1

parts:
  元件1 = Arduino Nano (Rev3.0)  # not connected
  IC1 = DS1302 [package="DIP8 [THT]"]
  U2 = RELAY-2 [package=relay-g5v]  # not connected
  U6 = Nokia 6100 Color LCD [package=nokia6100_lcd]  # not connected
  Y1 = CRYSTAL [package=tc26h]
  BAT2 = Battery Holders [package=battcom_20mm_pth]

nets:
  N1: IC1.X1_-_Crystal, Y1.1
  N2: IC1.X2_-_Crystal, Y1.2
  N3: IC1.0V, BAT2.-
  N4: IC1.Vbat_-_Backup_Supply, BAT2.+
